// Logisim project VLAB.circ as structural Verilog: 17 circuits, main circuit HalfAdder
module OR_3 (
  input  in_1,
  input  in_2,
  input  in_3,
  output out_4
);

  wire or_1_out;

  or or_1 (or_1_out, in_1, in_2);
  or or_2 (out_4, or_1_out, in_3);
endmodule

module OR_4 (
  input  in_1,
  input  in_2,
  input  in_3,
  input  in_4,
  output out_5
);

  wire or_1_out, or_2_out;

  or or_1 (or_1_out, in_1, in_2);
  or or_2 (or_2_out, in_3, in_4);
  or or_3 (out_5, or_1_out, or_2_out);
endmodule

module OR_5 (
  input  in_1,
  input  in_2,
  input  in_3,
  input  in_4,
  input  in_5,
  output out_6
);

  wire or_1_out, or_2_out, or_3_out;

  or or_1 (or_1_out, in_1, in_2);
  or or_2 (or_2_out, in_3, in_4);
  or or_3 (or_3_out, or_1_out, or_2_out);
  or or_4 (out_6, or_3_out, in_5);
endmodule

module AND_3 (
  input  in_1,
  input  in_2,
  input  in_3,
  output out_4
);

  wire and_1_out;

  and and_1 (and_1_out, in_1, in_2);
  and and_2 (out_4, and_1_out, in_3);
endmodule

module AND_4 (
  input  in_1,
  input  in_2,
  input  in_3,
  input  in_4,
  output out_5
);

  wire and_1_out, and_2_out;

  and and_1 (and_1_out, in_1, in_2);
  and and_2 (and_2_out, in_3, in_4);
  and and_3 (out_5, and_1_out, and_2_out);
endmodule

module AND_5 (
  input  in_1,
  input  in_2,
  input  in_3,
  input  in_4,
  input  in_5,
  output out_6
);

  wire and_1_out, and_2_out, and_3_out;

  and and_1 (and_1_out, in_1, in_2);
  and and_2 (and_2_out, in_3, in_4);
  and and_3 (and_3_out, and_1_out, and_2_out);
  and and_4 (out_6, and_3_out, in_5);
endmodule

module HalfAdder (
  input  X,
  input  Y,
  output Sum,
  output Carry
);

  xor xor_1 (Sum, X, Y);
  and and_1 (Carry, X, Y);
endmodule

module FullAdder (
  input  X,
  input  Y,
  input  Z,
  output Sum,
  output Carry
);

  wire HA1_carry, HA1_sum, HA2_carry;

  HalfAdder HA1 (.X(X), .Y(Y), .Sum(HA1_sum), .Carry(HA1_carry));
  HalfAdder HA2 (.X(HA1_sum), .Y(Z), .Sum(Sum), .Carry(HA2_carry));
  or or_1 (Carry, HA2_carry, HA1_carry);
endmodule

module RippleCarryAdder (
  input  Cin,
  input  A0,
  input  B0,
  input  A1,
  input  B1,
  input  A2,
  input  B2,
  input  A3,
  input  B3,
  output S0,
  output S1,
  output S2,
  output S3,
  output Cout
);

  wire fulladder_1_carry, fulladder_2_carry, fulladder_3_carry;

  FullAdder fulladder_1 (.X(Cin), .Y(A0), .Z(B0), .Sum(S0), .Carry(fulladder_1_carry));
  FullAdder fulladder_2 (.X(fulladder_1_carry), .Y(A1), .Z(B1), .Sum(S1), .Carry(fulladder_2_carry));
  FullAdder fulladder_3 (.X(fulladder_2_carry), .Y(A2), .Z(B2), .Sum(S2), .Carry(fulladder_3_carry));
  FullAdder fulladder_4 (.X(fulladder_3_carry), .Y(A3), .Z(B3), .Sum(S3), .Carry(Cout));
endmodule

module CarryLookAheadAdder (
  input  Cin,
  input  A0,
  input  B0,
  input  A1,
  input  B1,
  input  A2,
  input  B2,
  input  A3,
  input  B3,
  output S0,
  output S1,
  output S2,
  output S3,
  output Cout
);

  wire and_1_out, and_2_out, and_3_1_out_4, and_3_2_out_4, and_3_3_out_4, and_3_out, and_4_1_out_5,
       and_4_2_out_5, and_4_out, and_5_1_out_6, C1, C2, C3, G0, G1, G2, G3, P0, P1, P2, P3;

  HalfAdder halfadder_1 (.X(A0), .Y(B0), .Sum(P0), .Carry(G0));
  HalfAdder halfadder_2 (.X(A1), .Y(B1), .Sum(P1), .Carry(G1));
  HalfAdder halfadder_3 (.X(A2), .Y(B2), .Sum(P2), .Carry(G2));
  HalfAdder halfadder_4 (.X(A3), .Y(B3), .Sum(P3), .Carry(G3));
  and and_1 (and_1_out, Cin, P0);
  AND_3 and_3_1 (.in_2(P0), .in_3(Cin), .in_1(P1), .out_4(and_3_1_out_4));
  and and_2 (and_2_out, P1, G0);
  AND_4 and_4_1 (.in_3(P0), .in_4(Cin), .in_1(P2), .in_2(P1), .out_5(and_4_1_out_5));
  AND_3 and_3_2 (.in_2(P1), .in_3(G0), .in_1(P2), .out_4(and_3_2_out_4));
  and and_3 (and_3_out, P1, G1);
  AND_5 and_5_1 (.in_2(P2), .in_3(P1), .in_4(P0), .in_5(Cin), .in_1(P3), .out_6(and_5_1_out_6));
  AND_4 and_4_2 (.in_3(P1), .in_4(G0), .in_1(P3), .in_2(P2), .out_5(and_4_2_out_5));
  AND_3 and_3_3 (.in_2(P2), .in_3(G1), .in_1(P3), .out_4(and_3_3_out_4));
  and and_4 (and_4_out, P3, G2);
  or or_1 (C1, and_1_out, G0);
  OR_3 or_3_1 (.in_2(and_2_out), .in_3(G1), .in_1(and_3_1_out_4), .out_4(C2));
  OR_4 or_4_1 (.in_3(and_3_out), .in_4(G2), .in_1(and_4_1_out_5), .in_2(and_3_2_out_4), .out_5(C3));
  OR_5 or_5_1 (
    .in_2(and_4_2_out_5), .in_3(and_3_3_out_4), .in_4(and_4_out), .in_5(G3), .in_1(and_5_1_out_6),
    .out_6(Cout));
  xor xor_1 (S0, Cin, P0);
  xor xor_2 (S1, C1, P1);
  xor xor_3 (S2, C2, P2);
  xor xor_4 (S3, C3, P3);

  // Other names for the same wires on the sheet: C0 = Cin; C4 = Cout
endmodule

module WallaceTreeAdder (
  input  X0,
  input  Y0,
  input  Z0,
  input  X1,
  input  Y1,
  input  Z1,
  input  X2,
  input  Y2,
  input  Z2,
  input  X3,
  input  Y3,
  input  Z3,
  output S0,
  output S1,
  output S2,
  output S3,
  output S4,
  output S5
);

  wire C0, C1, C2, C3, not_1_out, not_2_out, S1_t, S2_t, S3_t;

  FullAdder fulladder_1 (.X(X0), .Y(Y0), .Z(Z0), .Sum(S0), .Carry(C0));
  FullAdder fulladder_2 (.X(X1), .Y(Y1), .Z(Z1), .Sum(S1_t), .Carry(C1));
  FullAdder fulladder_3 (.X(X2), .Y(Y2), .Z(Z2), .Sum(S2_t), .Carry(C2));
  FullAdder fulladder_4 (.X(X3), .Y(Y3), .Z(Z3), .Sum(S3_t), .Carry(C3));
  not not_1 (not_1_out, 1'b1);
  not not_2 (not_2_out, 1'b1);
  CarryLookAheadAdder carrylookaheadadder_1 (
    .A0(S1_t), .B0(C0), .A1(S2_t), .B1(C1), .A2(S3_t), .B2(C2), .Cin(not_1_out), .B3(C3), .A3(not_2_out),
    .Cout(S5), .S1(S2), .S2(S3), .S0(S1), .S3(S4));
endmodule

module SRLatch (
  input  S_bar,
  input  R_bar,
  input  CLR,
  output Q,
  output Q_not
);

  nand nand_1 (Q, S_bar, Q_not);
  nand nand_2 (Q_not, Q, CLR, R_bar);
endmodule

module EdgeDetector (
  input  Signal_In,
  output Pulse_Out
);

  wire not_1_out, not_2_out, not_3_out;

  not not_1 (not_1_out, Signal_In);
  not not_2 (not_2_out, not_1_out);
  and and_1 (Pulse_Out, Signal_In, not_3_out);
  not not_3 (not_3_out, not_2_out);
endmodule

module JKFlipFlop (
  input  in_1,
  input  in_2,
  output out_3,
  output out_4
);

  wire clock_1_out, edgedetector_1_pulse_out, nand_1_out, nand_2_out;

  Clock #(.highDuration(5), .lowDuration(5)) clock_1 (.out(clock_1_out));
  EdgeDetector edgedetector_1 (.Signal_In(clock_1_out), .Pulse_Out(edgedetector_1_pulse_out));
  nand nand_1 (nand_1_out, in_1, out_4, edgedetector_1_pulse_out);
  nand nand_2 (nand_2_out, edgedetector_1_pulse_out, out_3, in_2);
  SRLatch srlatch_1 (.R_bar(nand_2_out), .S_bar(nand_1_out), .Q(out_3), .Q_not(out_4));  // open: CLR
endmodule

module MasterSlaveJK (
  input  J,
  input  CLK,
  input  K,
  input  CLR,
  output Q,
  output Q_not
);

  wire nand_1_out, nand_2_out, nand_3_out, nand_4_out, nand_5_out, nand_6_out, not_1_out;

  nand nand_1 (nand_1_out, J, Q_not, CLK);
  nand nand_2 (nand_2_out, CLK, Q, K);
  not not_1 (not_1_out, CLK);
  nand nand_3 (nand_3_out, nand_1_out, nand_4_out);
  nand nand_4 (nand_4_out, nand_3_out, nand_2_out);
  nand nand_5 (nand_5_out, nand_3_out, not_1_out);
  nand nand_6 (nand_6_out, not_1_out, nand_4_out);
  nand nand_7 (Q, nand_5_out, Q_not);
  nand nand_8 (Q_not, Q, CLR, nand_6_out);
endmodule

module DFlipFlop (
  input  D,
  input  CLK,
  input  CLR,
  output Q,
  output Q_not
);

  wire not_1_out;

  not not_1 (not_1_out, D);
  MasterSlaveJK masterslavejk_1 (.J(D), .CLK(CLK), .K(not_1_out), .CLR(CLR), .Q(Q), .Q_not(Q_not));
endmodule

module TFlipFlop (
  input  T,
  input  CLK,
  input  CLR,
  output Q,
  output Q_not
);

  MasterSlaveJK masterslavejk_1 (.J(T), .CLK(CLK), .K(T), .CLR(CLR), .Q(Q), .Q_not(Q_not));
endmodule
